# Fritzing sketch Heizverteiler (saved by Fritzing 0.9.10b)
perfboards: 1

parts:
  MH-ET_LIVE_ESP32_DEVKIT1 = MH-ET LIVE ESP32 DEVKIT 38 pins
  HLK-PM1 = HLK-PM01
  8_Channel_Relay2 = 8 Channel Power Relay
  U9 = Hirose DF13 Series Header [part_number=DF13#-3P-1.25V package=DF13C-3P-1.25V]
  DS9 = DS18B20 1-Wire Temperature Sensor [part_number=DS18B20]
  DS11 = DS18B20 1-Wire Temperature Sensor [part_number=DS18B20]  # not connected
  DS12 = DS18B20 1-Wire Temperature Sensor [part_number=DS18B20]  # not connected
  DS13 = DS18B20 1-Wire Temperature Sensor [part_number=DS18B20]  # not connected
  DS14 = DS18B20 1-Wire Temperature Sensor [part_number=DS18B20]  # not connected
  DS15 = DS18B20 1-Wire Temperature Sensor [part_number=DS18B20]  # not connected
  DS16 = DS18B20 1-Wire Temperature Sensor [part_number=DS18B20]
  R2 = Resistor [tolerance=±5% resistance=220 package="1206 [SMD]"]

nets:
  3V3: MH-ET_LIVE_ESP32_DEVKIT1.3V3, 8_Channel_Relay2.VCC
  N1: MH-ET_LIVE_ESP32_DEVKIT1.IO33, 8_Channel_Relay2.IN6
  N2: MH-ET_LIVE_ESP32_DEVKIT1.IO25, 8_Channel_Relay2.IN5
  N3: MH-ET_LIVE_ESP32_DEVKIT1.IO26, 8_Channel_Relay2.IN4
  N4: MH-ET_LIVE_ESP32_DEVKIT1.IO27, 8_Channel_Relay2.IN3
  N5: MH-ET_LIVE_ESP32_DEVKIT1.IO14, 8_Channel_Relay2.IN2
  N6: MH-ET_LIVE_ESP32_DEVKIT1.IO12, 8_Channel_Relay2.IN1
  N7: MH-ET_LIVE_ESP32_DEVKIT1.GND#58, 8_Channel_Relay2.GND#8
  N8: MH-ET_LIVE_ESP32_DEVKIT1.IO13, 8_Channel_Relay2.IN8
  N9: MH-ET_LIVE_ESP32_DEVKIT1.5V, 8_Channel_Relay2.JD-VCC
  GND: MH-ET_LIVE_ESP32_DEVKIT1.GND#70, DS9.GND, DS16.GND
  N10: MH-ET_LIVE_ESP32_DEVKIT1.IO16, 8_Channel_Relay2.IN7
  N11: MH-ET_LIVE_ESP32_DEVKIT1.IO4, DS9.DQ, DS16.DQ, R2.Pin_0
  N12: HLK-PM1.-Vo, U9.2
  N13: HLK-PM1.+Vo, U9.3
  VDD: DS9.VDD, DS16.VDD

custom parts:
  MH-ET LIVE ESP32 DEVKIT 38 pins: http://mh.nodebb.com/topic/2/mh-et-live-esp32-devkit
  8 Channel Power Relay: An 8 channel power relay. The module operates at 5V.
