# Fritzing sketch heitverteiler (saved by Fritzing 0.9.10b)

parts:
  J1 = shrouded pin header, 10 pins [form="♂ (shrouded male)"]
  MH-ET_LIVE_ESP32_DEVKIT1 = MH-ET LIVE ESP32 DEVKIT 38 pins
  IC1 = MCP23017 I2C I/O Expander
  J2 = shrouded pin header, 10 pins [form="♂ (shrouded male)"]
  HLK-PM1 = HLK-PM12 [part_number=HLK-PM12]
  J3 = Camdenboss CTB0158-2 [part_number=CTB0158-2 package=THT]
  8_Channel_Relay1 = 8 Channel Power Relay
  J4 = Camdenboss CTB0158-2 [part_number=CTB0158-2 package=THT]
  J5 = Camdenboss CTB0158-2 [part_number=CTB0158-2 package=THT]
  J6 = Camdenboss CTB0158-2 [part_number=CTB0158-2 package=THT]
  J7 = Camdenboss CTB0158-2 [part_number=CTB0158-2 package=THT]
  J8 = Camdenboss CTB0158-2 [part_number=CTB0158-2 package=THT]
  J9 = Camdenboss CTB0158-2 [part_number=CTB0158-2 package=THT]
  J10 = Camdenboss CTB0158-2 [part_number=CTB0158-2 package=THT]
  J11 = Camdenboss CTB0158-2 [part_number=CTB0158-2 package=THT]

nets:
  GND: J1.pin1, MH-ET_LIVE_ESP32_DEVKIT1.GND, IC1.VSS, IC1.A0, IC1.A1, IC1.A2, J2.pin1, HLK-PM1.-Vo
  N1: J1.pin2, IC1.GPB0
  N2: J1.pin3, IC1.GPB1
  N3: J1.pin4, IC1.GPB2
  N4: J1.pin5, IC1.GPB3
  N5: J1.pin6, IC1.GPB4
  N6: J1.pin7, IC1.GPB5
  N7: J1.pin8, IC1.GPB6
  N8: J1.pin9, IC1.GPB7
  5V: J1.pin10, MH-ET_LIVE_ESP32_DEVKIT1.5V, IC1.VDD, IC1.RESET, J2.pin10, HLK-PM1.+Vo
  N9: MH-ET_LIVE_ESP32_DEVKIT1.IO22, IC1.SCL
  N10: MH-ET_LIVE_ESP32_DEVKIT1.IO21, IC1.SDA
  N11: IC1.GPA0, J2.pin2
  N12: IC1.GPA1, J2.pin3
  N13: IC1.GPA2, J2.pin4
  N14: IC1.GPA3, J2.pin5
  N15: IC1.GPA4, J2.pin6
  N16: IC1.GPA5, J2.pin7
  N17: IC1.GPA6, J2.pin8
  N18: IC1.GPA7, J2.pin9
  N19: HLK-PM1.AC_1, J3.pin2
  N20: HLK-PM1.AC_2, J3.pin1
  N21: J3.terminal_1, 8_Channel_Relay1.COM
  N22: J3.terminal_2, J4.terminal_2, J5.terminal_2, J6.terminal_2, J7.terminal_2, J8.terminal_2, J9.terminal_2, J10.terminal_2, J11.terminal_2
  N23: 8_Channel_Relay1.NO#23, J4.terminal_1
  N24: 8_Channel_Relay1.NO#26, J5.terminal_1
  N25: 8_Channel_Relay1.NO#29, J6.terminal_1
  N26: 8_Channel_Relay1.NO#32, J7.terminal_1
  N27: 8_Channel_Relay1.NO#35, J8.terminal_1
  N28: 8_Channel_Relay1.NO#38, J9.terminal_1
  N29: 8_Channel_Relay1.NO#41, J10.terminal_1
  N30: 8_Channel_Relay1.NO#44, J11.terminal_1

custom parts:
  MH-ET LIVE ESP32 DEVKIT 38 pins: http://mh.nodebb.com/topic/2/mh-et-live-esp32-devkit
  MCP23017 I2C I/O Expander: The MCP23017 uses two i2c pins (these can be shared with other i2c devices), and in exchange gives you 16 general purpose pins. You can set each of 16 pins to be input, output, input with a pullup or open drain. There's even the ability to get an interrupt via an external pin when any of the inputs change so you don't have to keep polling the chip.
  8 Channel Power Relay: An 8 channel power relay. The module operates at 5V.
