# Fritzing sketch WandController (saved by Fritzing 0.9.10b)

parts:
  MH-ET_LIVE_ESP32_DEVKIT1 = MH-ET LIVE ESP32 DEVKIT 38 pins
  LCD1 = 2.8" SPI TFT Module [part_number=MSP2807]
  DHT1 = Humidity and Temperature Sensor DHT11
  R1 = Resistor [tolerance=±5% resistance=10k package="1206 [SMD]"]
  S1 = Momentary Switch [package=tactile-pth]
  S2 = Momentary Switch [package=tactile-pth]
  U1 = LIPO-1000mAh [package=lipo-1000]
  R2 = Resistor [tolerance=±5% resistance=47k package="1206 [SMD]"]
  R3 = Resistor [tolerance=±5% resistance=47k package="1206 [SMD]"]
  TP1 = TP4056 [chip_label=TP4056 package="DIP (Dual Inline) [THT]"]
  M1 = MT3608 Module

nets:
  3V3: MH-ET_LIVE_ESP32_DEVKIT1.3V3, DHT1.Vcc, R1.Pin_1
  N1: MH-ET_LIVE_ESP32_DEVKIT1.IO34, R2.Pin_0, R3.Pin_0
  N2: MH-ET_LIVE_ESP32_DEVKIT1.IO35, S2.1
  N3: MH-ET_LIVE_ESP32_DEVKIT1.IO32, S1.1
  N4: MH-ET_LIVE_ESP32_DEVKIT1.IO33, LCD1.pin11
  N5: MH-ET_LIVE_ESP32_DEVKIT1.IO25, LCD1.pin14
  N6: MH-ET_LIVE_ESP32_DEVKIT1.IO26, LCD1.pin5
  N7: MH-ET_LIVE_ESP32_DEVKIT1.IO27, LCD1.pin3
  N8: MH-ET_LIVE_ESP32_DEVKIT1.IO12, DHT1.Data-signal, R1.Pin_0
  N9: MH-ET_LIVE_ESP32_DEVKIT1.GND, LCD1.pin2, DHT1.GND_2, S1.4, S2.4, M1.pin4
  N10: MH-ET_LIVE_ESP32_DEVKIT1.5V, LCD1.pin1, M1.pin3
  N11: MH-ET_LIVE_ESP32_DEVKIT1.IO23, LCD1.pin6, LCD1.pin12
  N12: MH-ET_LIVE_ESP32_DEVKIT1.IO19, LCD1.pin9, LCD1.pin13
  N13: MH-ET_LIVE_ESP32_DEVKIT1.IO18, LCD1.pin7, LCD1.pin10
  N14: MH-ET_LIVE_ESP32_DEVKIT1.IO5, LCD1.pin4
  N15: MH-ET_LIVE_ESP32_DEVKIT1.IO4, LCD1.pin8
  N16: U1.+, R3.Pin_1, TP1.pin3, M1.pin2
  N17: U1.-, R2.Pin_1, TP1.pin6, M1.pin1

custom parts:
  MH-ET LIVE ESP32 DEVKIT 38 pins: http://mh.nodebb.com/topic/2/mh-et-live-esp32-devkit
  2.8" SPI TFT Module: A generic 2.8 inch LCD TFT 320x240 display with touchscreen and SD card slot. Uses the ILI9341 controller, like the Adafruit displays of this size uses.
  Humidity and Temperature Sensor DHT11: Digital relative humidity & temperature sensor DHT11
  TP4056: A DIP stand-in part for whatever IC you want. With 6 pins on a 300mil dual inline package (DIP) footprint.
  MT3608 Module: MT3608 Boost Converter Module Links: Aerosemi MT3608 2A Step Up Converter datasheet
