# Fritzing sketch WandController2 (saved by Fritzing 0.9.10b)

parts:
  MH-ET_LIVE_ESP32_DEVKIT1 = MH-ET LIVE ESP32 DEVKIT 38 pins
  LCD1 = 2.8" SPI TFT Module [part_number=MSP2807]

nets:
  N1: MH-ET_LIVE_ESP32_DEVKIT1.IO32, LCD1.pin8
  N2: MH-ET_LIVE_ESP32_DEVKIT1.GND, LCD1.pin2
  N3: MH-ET_LIVE_ESP32_DEVKIT1.5V, LCD1.pin1
  N4: MH-ET_LIVE_ESP32_DEVKIT1.IO23, LCD1.pin6, LCD1.pin12
  N5: MH-ET_LIVE_ESP32_DEVKIT1.IO21, LCD1.pin11
  N6: MH-ET_LIVE_ESP32_DEVKIT1.IO19, LCD1.pin13
  N7: MH-ET_LIVE_ESP32_DEVKIT1.IO18, LCD1.pin7, LCD1.pin10
  N8: MH-ET_LIVE_ESP32_DEVKIT1.IO16, LCD1.pin14
  N9: MH-ET_LIVE_ESP32_DEVKIT1.IO4, LCD1.pin4
  N10: MH-ET_LIVE_ESP32_DEVKIT1.IO2, LCD1.pin5
  N11: MH-ET_LIVE_ESP32_DEVKIT1.IO15, LCD1.pin3

custom parts:
  MH-ET LIVE ESP32 DEVKIT 38 pins: http://mh.nodebb.com/topic/2/mh-et-live-esp32-devkit
  2.8" SPI TFT Module: A generic 2.8 inch LCD TFT 320x240 display with touchscreen and SD card slot. Uses the ILI9341 controller, like the Adafruit displays of this size uses.
